# Fritzing sketch FritzingSchema-RingMode (saved by Fritzing 0.9.3b)
circuit board: 20.5cm x 27cm
breadboards: 1

parts:
  Componente1 = Adafruit Circuit Playground Express [part_number="Adafruit #3333"]
  S1 = Textile Pushbutton [part_number="TACRACPS1X0404GY "]
  S2 = Textile Pushbutton [part_number="TACRACPS1X0404GY "]
  S3 = Textile Pushbutton [part_number="TACRACPS1X0404GY "]
  S4 = Textile Pushbutton [part_number="TACRACPS1X0404GY "]
  LED1 = Adafruit FLORA NeoPixel RememBag V1
  LED2 = Adafruit FLORA NeoPixel RememBag V1
  LED3 = Adafruit FLORA NeoPixel RememBag V1
  LED4 = Adafruit FLORA NeoPixel RememBag V1

nets:
  N1: Componente1.3.3V, S1.leg0, S2.leg0, S3.leg0, S4.leg0, LED1.V+, LED2.V+, LED3.V+, LED4.V+
  N2: Componente1.D6_A1, S3.leg1
  GND: Componente1.GND, LED1.GND, LED2.GND, LED3.GND, LED4.GND
  N3: Componente1.D10_A3, S4.leg1
  N4: Componente1.D3_A4_SCL, LED1.IN
  N5: Componente1.D2_A5_SDA, S1.leg1
  N6: Componente1.D1_A7_TX, S2.leg1
  N7: LED1.OUT, LED2.IN
  N8: LED2.OUT, LED3.IN
  N9: LED3.OUT, LED4.IN

custom parts:
  Adafruit Circuit Playground Express: Circuit Playground Express is the next step towards a perfect introduction to electronics and programming. We've taken the original Circuit Playground Classic and made it even better! Not only did we pack even more sensors in, we also made it even easier to program. You can now start your journey with Microsoft MakeCode block-based or Javascript programming. Then, you can use the same board to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
  Adafruit FLORA NeoPixel RememBag V1: Adafruit FLORA RGB Smart Pixel
